// Logisim project ArchiProc.circ as structural Verilog: 5 circuits, main circuit main
module main (
);

  wire clk_out, instdecoder_1_isjmp, instdecoder_1_isload, instdecoder_1_regwrite, RESET_out;
  wire [2:0] instdecoder_1_ctrual;
  wire [3:0] ual_1_flags, undriven, undriven_2, undriven_3, undriven_4;
  wire [7:0] multiplexer_1_out, regbank_1_rs_2, regbank_1_rt_2, ual_1_res, undriven_5;

  Button RESET (.out(RESET_out));
  Clock clk (.out(clk_out));
  instDecoder instdecoder_1 (
    .opcode(undriven), .isLoad(instdecoder_1_isload), .ctrUAL(instdecoder_1_ctrual),
    .isJMP(instdecoder_1_isjmp), .regWrite(instdecoder_1_regwrite));
  regBank regbank_1 (
    .RESET(RESET_out), .regWrite(instdecoder_1_regwrite), .clk(clk_out), .valIn(multiplexer_1_out),
    .Rs_2(regbank_1_rs_2), .Rt_2(regbank_1_rt_2), .Rd(undriven_2), .Rs(undriven_3), .Rt(undriven_4));
  Multiplexer #(.width(8), .enable("false")) multiplexer_1 (
    .in0(ual_1_res), .in1(undriven_5), .out(multiplexer_1_out), .sel(instdecoder_1_isload));
  UAL ual_1 (
    .Rs(regbank_1_rs_2), .Rt(regbank_1_rt_2), .res(ual_1_res), .flags(ual_1_flags),
    .ctrUAL(instdecoder_1_ctrual));
endmodule

module UAL (
  input  [7:0] Rs,
  input  [2:0] ctrUAL,
  input  [7:0] Rt,
  output [3:0] flags,
  output [7:0] res
);

  wire adder_1_cout, OF, or_3_out, subtractor_1_bout;
  wire [2:0] bitselector_1_out;
  wire [7:0] adder_1_out, and_1_out, not_1_out, or_1_out, shifter_1_out, shifter_2_out, subtractor_1_out;

  BitSelector #(.group(3)) bitselector_1 (.in(Rt), .out(bitselector_1_out), .sel(2'b00));
  Adder adder_1 (.a(Rs), .b(Rt), .out(adder_1_out), .cout(adder_1_cout));  // open: cin
  Subtractor subtractor_1 (.a(Rs), .b(Rt), .out(subtractor_1_out), .bout(subtractor_1_bout));  // open: bin
  assign or_1_out = Rs | Rt;  // OR_Gate or_1, 8 bits wide
  assign and_1_out = Rs & Rt;  // AND_Gate and_1, 8 bits wide
  assign not_1_out = ~Rs;  // NOT_Gate not_1, 8 bits wide
  Shifter shifter_1 (.in(Rs), .\dist (bitselector_1_out), .out(shifter_1_out));
  Shifter #(.shift("lr")) shifter_2 (.in(Rs), .\dist (bitselector_1_out), .out(shifter_2_out));
  or or_2 (OF, Rs[7], Rt[7]);
  Multiplexer #(.select(3), .enable("false")) multiplexer_1 (
    .in0(adder_1_cout), .in1(subtractor_1_bout), .in2(1'b0), .in3(1'b0), .in4(1'b0), .in5(1'b0), .in6(1'b0),
    .out(flags[3]), .sel(ctrUAL));  // open: in7
  or or_3 (or_3_out, res[0], res[1], res[2], res[3], res[4], res[5], res[6], flags[1]);
  not not_2 (flags[2], or_3_out);
  Multiplexer #(.select(3), .width(8), .enable("false")) multiplexer_2 (
    .in0(adder_1_out), .in1(subtractor_1_out), .in2(or_1_out), .in3(and_1_out), .in4(not_1_out),
    .in5(shifter_1_out), .in6(shifter_2_out), .out({flags[1], res[6:0]}), .sel(ctrUAL));  // open: in7
  xor xor_1 (flags[0], flags[1], OF);

  assign res[7] = flags[1];

  // Other names for the same wires on the sheet: CF[2:0] = ctrUAL; SF[7:0] = {flags[1], res[6:0]};
  //   ZF[7:0] = {flags[1], res[6:0]}
endmodule

module instDecoder (
  input  [3:0] opcode,
  output isJMP,
  output regWrite,
  output isLoad,
  output [2:0] ctrUAL
);

  wire and_1_out, and_2_out, and_3_out;

  and and_1 (and_1_out, opcode[3], opcode[2]);
  or or_1 (isJMP, and_1_out, and_2_out, and_3_out);
  and and_2 (and_2_out, opcode[3], ~opcode[1], opcode[0]);  // AND_Gate
  and and_3 (and_3_out, opcode[3], opcode[1]);
  not not_1 (regWrite, opcode[3]);
  and and_4 (isLoad, ~opcode[3], opcode[2], opcode[1], opcode[0]);  // AND_Gate

  assign ctrUAL = opcode[2:0];

  // Notes on the sheet:
  //   Probablement nécessaire de jeter un oeil sur le décodeur d'instructions par rapport au renvoi à l'UAL quand un saut a lieu
endmodule

module jmpController (
  input  [3:0] flags,
  input  [3:0] opcode,
  output [1:0] nextPCselect
);


  // Notes on the sheet:
  //   On code 00 : "HALT"
  //   01 : "instruction suivante"
  //   10 : "saut"
endmodule

module regBank (
  input  [3:0] Rd,
  input  [3:0] Rs,
  input  [3:0] Rt,
  input  RESET,
  input  regWrite,
  input  clk,
  input  [7:0] valIn,
  output [7:0] Rs_2,
  output [7:0] Rt_2
);

  Register register_1 (.clk(clk), .clr(RESET));  // open: D, en, Q
  Register register_2 (.clk(clk), .clr(RESET));  // open: D, en, Q
  Register register_3 (.clk(clk), .clr(RESET));  // open: D, en, Q
  Register register_4 (.clk(clk), .clr(RESET));  // open: D, en, Q
  Register register_5 (.clk(clk), .clr(RESET));  // open: D, en, Q
  Register register_6 (.clk(clk), .clr(RESET));  // open: D, en, Q
  Register register_7 (.clk(clk), .clr(RESET));  // open: D, en, Q
  Register register_8 (.clk(clk), .clr(RESET));  // open: D, en, Q
  Register register_9 (.clk(clk), .clr(RESET));  // open: D, en, Q
  Register register_10 (.clk(clk), .clr(RESET));  // open: D, en, Q
  Register register_11 (.clk(clk), .clr(RESET));  // open: D, en, Q
  Register register_12 (.clk(clk), .clr(RESET));  // open: D, en, Q
  Register register_13 (.clk(clk), .clr(RESET));  // open: D, en, Q
  Register register_14 (.clk(clk), .clr(RESET));  // open: D, en, Q
  Register register_15 (.clk(clk), .clr(RESET));  // open: D, en, Q
  Register register_16 (.clk(clk), .clr(RESET));  // open: D, en, Q
endmodule
